// Logisim project ISA.circ as structural Verilog: 1 circuit, main circuit my circuit
module my_circuit (
  input  [31:0] in_1,
  input  LD_PC,
  input  LD_MAR,
  output [31:0] out_4
);

  wire [31:0] PC_q;

  Register #(.width(32)) PC (.D(in_1), .Q(PC_q), .clk(LD_PC));  // open: en, clr
  Register #(.width(32)) MAR (.D(PC_q), .Q(out_4), .clk(LD_MAR));  // open: en, clr
endmodule
